# Fritzing sketch tree_of_flow (saved by Fritzing 0.8.7b)
breadboards: 1

parts:
  Bauteil1 = Arduino Uno (Rev3)
  R1 = Resistor [tolerance=±5% resistance=1 package=THT]
  LED1 = LED - 5mm [color="Orange (612nm)" package="5 mm [THT]"]
  LED2 = LED - 5mm [color="Orange (612nm)" package="5 mm [THT]"]
  LED3 = LED - 5mm [color="Orange (612nm)" package="5 mm [THT]"]
  LED4 = LED - 5mm [color="Orange (612nm)" package="5 mm [THT]"]
  LED5 = LED - 5mm [color="Orange (612nm)" package="5 mm [THT]"]
  LED6 = LED - 5mm [color="Orange (612nm)" package="5 mm [THT]"]
  R2 = Resistor [tolerance=±20% resistance=220 package=THT]
  R3 = Resistor [tolerance=±20% resistance=220 package=THT]
  R4 = Resistor [tolerance=±20% resistance=220 package=THT]
  R5 = Resistor [tolerance=±20% resistance=220 package=THT]
  R6 = Resistor [tolerance=±20% resistance=220 package=THT]
  R7 = Resistor [tolerance=±20% resistance=220 package=THT]

nets:
  N1: Bauteil1.D9_PWM, LED4.anode
  N2: Bauteil1.D10_PWM/SS, LED5.anode
  N3: Bauteil1.D11_PWM/MOSI, LED6.anode
  N4: Bauteil1.D2, R1.Pin_1
  N5: Bauteil1.D3_PWM, LED1.anode
  N6: Bauteil1.D4, R1.Pin_0
  N7: Bauteil1.D5_PWM, LED2.anode
  N8: Bauteil1.D6_PWM, LED3.anode
  N9: Bauteil1.GND, R2.Pin_1, R3.Pin_1, R4.Pin_1, R5.Pin_1, R6.Pin_1, R7.Pin_1
  N10: LED1.cathode, R7.Pin_0
  N11: LED2.cathode, R6.Pin_0
  N12: LED3.cathode, R2.Pin_0
  N13: LED4.cathode, R3.Pin_0
  N14: LED5.cathode, R4.Pin_0
  N15: LED6.cathode, R5.Pin_0
